// Logisim project 디지털공학 논리회로 숫자.circ as structural Verilog: 1 circuit, main circuit main
module main (
  input  A,
  input  B,
  input  C,
  input  D
);

  wire A_prime_B_prime_C_out, AB_prime_out, B_prime_C_out, B_prime_D_prime_out, BC_prime_D_out, BC_prime_out,
       BD_out, C_prime_D_prime_out, CD_out, CD_prime_out, not_1_out, not_2_out, not_3_out, not_4_out,
       not_5_out, not_6_out, or_1_out, or_2_out, or_3_out, or_4_out, or_5_out, or_6_out, or_7_out;

  not not_1 (not_1_out, A);
  not not_2 (not_2_out, B);
  not not_3 (not_3_out, B);
  not not_4 (not_4_out, D);
  not not_5 (not_5_out, D);
  not not_6 (not_6_out, C);
  and BD (BD_out, B, D);
  and B_prime_D_prime (B_prime_D_prime_out, not_3_out, not_4_out);
  and AB_prime (AB_prime_out, A, not_2_out);
  and CD_prime (CD_prime_out, C, not_5_out);
  and A_prime_B_prime_C (A_prime_B_prime_C_out, not_2_out, not_1_out, C);
  and BC_prime (BC_prime_out, B, not_6_out);
  and B_prime_C (B_prime_C_out, not_2_out, C);
  and BC_prime_D (BC_prime_D_out, not_6_out, B, D);
  and C_prime_D_prime (C_prime_D_prime_out, not_6_out, not_4_out);
  and CD (CD_out, C, D);
  or or_1 (or_1_out, A, B_prime_D_prime_out, BD_out, C);
  or or_2 (or_2_out, AB_prime_out, CD_prime_out, B_prime_C_out, BC_prime_out);
  or or_3 (or_3_out, A, A_prime_B_prime_C_out, CD_prime_out, B_prime_D_prime_out, BC_prime_D_out);
  or or_4 (or_4_out, not_2_out, C_prime_D_prime_out, CD_out);
  or or_5 (or_5_out, D, A, B, not_6_out);
  or or_6 (or_6_out, A, B, C_prime_D_prime_out);
  or or_7 (or_7_out, B_prime_D_prime_out, CD_prime_out);
  _7_Segment_Display u_7_segment_display_1 (
    .g(or_2_out), .f(or_6_out), .a(or_1_out), .b(or_4_out), .e(or_7_out), .d(or_3_out), .c(or_5_out));  // open: dp

  // Notes on the sheet:
  //   A'
  //   B'
  //   D'
  //   C'
  //   a
  //   b
  //   c
  //   d
  //   e
  //   f
  //   g
endmodule
